// Logisim project P3 Main.circ as structural Verilog: 11 circuits, main circuit main
module main (
  input  areset,
  output [31:0] instruction,
  output RegWrite,
  output [4:0] RegAddr,
  output [31:0] RegData,
  output MemWrite,
  output [4:0] MemAddr,
  output [31:0] MemData
);

  wire aluData2REG_IMM, branch, clock_1_out, condition, controller_1_hasfunct, DMreadEnable, jump, true,
       writeRegDataALU_DM, writeRegRD_RT, zero_signEXT;
  wire [2:0] alucontroller_1_aluop, controller_1_aluvector;
  wire [4:0] instructionspliter_1_rd, instructionspliter_1_rs_base, instructionspliter_1_rt;
  wire [5:0] instructionspliter_1_funct, instructionspliter_1_opcode;
  wire [15:0] instructionspliter_1_imm;
  wire [25:0] jumpAddr;
  wire [31:0] ALUResult, bit_extender_1_out, bit_extender_2_out, DMout, grf_1_regdata1, multiplexer_4_out,
       relativeAddr;

  Clock clock_1 (.out(clock_1_out));
  // Probe on instruction
  IFU ifu_1 (
    .relativeAddr(relativeAddr), .condition(condition), .instruction(instruction), .clk(clock_1_out),
    .areset(areset), .jumpAddr(jumpAddr), .jump(jump));  // open: PC
  // Probe on instructionspliter_1_opcode
  Controller controller_1 (
    .opCode(instructionspliter_1_opcode), .writeRegSel(writeRegRD_RT), .writeRegDataSel(writeRegDataALU_DM),
    .aluData2Sel(aluData2REG_IMM), .branch(branch), .GRFwriteEnable(RegWrite), .DMwriteEnable(MemWrite),
    .DMreadEnable(DMreadEnable), .hasFunct(controller_1_hasfunct), .ALUvector(controller_1_aluvector),
    .zero_signEXT(zero_signEXT), .jump(jump));
  InstructionSpliter instructionspliter_1 (
    .instruction(instruction), .imm(instructionspliter_1_imm), .funct(instructionspliter_1_funct),
    .rd(instructionspliter_1_rd), .rt(instructionspliter_1_rt), .rs_base(instructionspliter_1_rs_base),
    .opCode(instructionspliter_1_opcode), .jumpAddr(jumpAddr));  // open: shamt
  ALUController alucontroller_1 (
    .hasFunct(controller_1_hasfunct), .ALUvector(controller_1_aluvector), .funct(instructionspliter_1_funct),
    .ALUOp(alucontroller_1_aluop));
  and and_1 (condition, true, branch);
  assign bit_extender_1_out = {{16{1'b0}}, instructionspliter_1_imm};  // Bit_Extender bit_extender_1
  assign bit_extender_2_out = {{16{instructionspliter_1_imm[15]}}, instructionspliter_1_imm};  // Bit_Extender bit_extender_2
  Multiplexer #(.width(32)) multiplexer_1 (
    .in0(bit_extender_1_out), .in1(bit_extender_2_out), .out(relativeAddr), .sel(zero_signEXT));  // open: en
  Multiplexer #(.width(5)) multiplexer_2 (
    .in0(instructionspliter_1_rd), .in1(instructionspliter_1_rt), .out(RegAddr), .sel(writeRegRD_RT));  // open: en
  Multiplexer #(.width(32)) multiplexer_3 (
    .in0({ALUResult[31:7], MemAddr, ALUResult[1:0]}), .in1(DMout), .out(RegData), .sel(writeRegDataALU_DM));  // open: en
  GRF grf_1 (
    .readReg1(instructionspliter_1_rs_base), .readReg2(instructionspliter_1_rt), .writeReg(RegAddr),
    .writeData(RegData), .regData1(grf_1_regdata1), .regData2(MemData), .clk(clock_1_out), .areset(areset),
    .writeEnable(RegWrite));
  ALU alu_1 (
    .data1(grf_1_regdata1), .data2(multiplexer_4_out), .equal(true),
    .result({ALUResult[31:7], MemAddr, ALUResult[1:0]}), .operation(alucontroller_1_aluop));
  Multiplexer #(.width(32)) multiplexer_4 (
    .in0(MemData), .in1(relativeAddr), .out(multiplexer_4_out), .sel(aluData2REG_IMM));  // open: en
  RAM #(.addrWidth(5), .dataWidth(32), .bus("separate")) ram_1 (
    .addr(MemAddr), .din(MemData), .data(DMout), .str(MemWrite), .clk(clock_1_out), .ld(DMreadEnable),
    .clr(areset));  // open: sel

  // Other names for the same wires on the sheet: DMwriteEnable = MemWrite; GRFwriteEnable = RegWrite;
  //   ALUResult[6:2] = MemAddr

  // Notes on the sheet:
  //   rd
  //   rt
  //   ALUResult
  //   DM
  //   rs(base)
  //   rt
  //   imm
  //   ALUSrc
  //   ALUOp
endmodule

module GRF (
  input  clk,
  input  areset,
  input  writeEnable,
  input  [4:0] readReg1,
  input  [4:0] readReg2,
  input  [4:0] writeReg,
  input  [31:0] writeData,
  output [31:0] regData1,
  output [31:0] regData2
);

  wire _0_writer, _1_writer, _2_writer, _3_writer, _4_writer, _5_writer, _6_writer, _7_writer, _8_writer,
       _9_writer, _10_writer, _11_writer, _12_writer, _13_writer, _14_writer, _15_writer, _16_writer,
       _17_writer, _18_writer, _19_writer, _20_writer, _21_writer, _22_writer, _23_writer, _24_writer,
       _25_writer, _26_writer, _27_writer, _28_writer, _29_writer, _30_writer, _31_writer, and_1_out,
       and_2_out, and_3_out, and_4_out, and_5_out, and_6_out, and_7_out, and_8_out, and_9_out, and_10_out,
       and_11_out, and_12_out, and_13_out, and_14_out, and_15_out, and_16_out, and_17_out, and_18_out,
       and_19_out, and_20_out, and_21_out, and_22_out, and_23_out, and_24_out, and_25_out, and_26_out,
       and_27_out, and_28_out, and_29_out, and_30_out, and_31_out, and_32_out;
  wire [31:0] _0_out, _1_out, _2_out, _3_out, _4_out, _5_out, _6_out, _7_out, _8_out, _9_out, _10_out,
       _11_out, _12_out, _13_out, _14_out, _15_out, _16_out, _17_out, _18_out, _19_out, _20_out, _21_out,
       _22_out, _23_out, _24_out, _25_out, _26_out, _27_out, _28_out, _29_out, _30_out, _31_out,
       multiplexer_1_out, multiplexer_2_out, multiplexer_3_out, multiplexer_4_out, multiplexer_5_out,
       multiplexer_6_out, multiplexer_7_out, multiplexer_8_out, multiplexer_9_out, multiplexer_10_out,
       multiplexer_11_out, multiplexer_12_out, multiplexer_13_out, multiplexer_14_out, multiplexer_15_out,
       multiplexer_16_out, multiplexer_17_out, multiplexer_18_out, multiplexer_19_out, multiplexer_20_out,
       multiplexer_21_out, multiplexer_22_out, multiplexer_23_out, multiplexer_24_out, multiplexer_27_out,
       multiplexer_28_out, multiplexer_29_out, multiplexer_30_out, multiplexer_31_out, multiplexer_32_out,
       multiplexer_33_out, multiplexer_34_out;

  Multiplexer #(.width(32)) multiplexer_1 (
    .in0(_0_out), .in1(writeData), .out(multiplexer_1_out), .sel(and_1_out));  // open: en
  Register #(.width(32)) register_1 (.D(multiplexer_1_out), .Q(_0_out), .clk(clk), .clr(1'b1));  // open: en
  and and_1 (and_1_out, _0_writer, writeEnable);
  Register #(.width(32)) register_2 (.D(multiplexer_2_out), .Q(_1_out), .clk(clk), .clr(areset));  // open: en
  Multiplexer #(.width(32)) multiplexer_2 (
    .in0(_1_out), .in1(writeData), .out(multiplexer_2_out), .sel(and_2_out));  // open: en
  and and_2 (and_2_out, _1_writer, writeEnable);
  Multiplexer #(.width(32)) multiplexer_3 (
    .in0(_2_out), .in1(writeData), .out(multiplexer_3_out), .sel(and_3_out));  // open: en
  Register #(.width(32)) register_3 (.D(multiplexer_3_out), .Q(_2_out), .clk(clk), .clr(areset));  // open: en
  and and_3 (and_3_out, _2_writer, writeEnable);
  Multiplexer #(.width(32)) multiplexer_4 (
    .in0(_3_out), .in1(writeData), .out(multiplexer_4_out), .sel(and_4_out));  // open: en
  Register #(.width(32)) register_4 (.D(multiplexer_4_out), .Q(_3_out), .clk(clk), .clr(areset));  // open: en
  and and_4 (and_4_out, _3_writer, writeEnable);
  Multiplexer #(.width(32)) multiplexer_5 (
    .in0(_16_out), .in1(writeData), .out(multiplexer_5_out), .sel(and_5_out));  // open: en
  Register #(.width(32)) register_5 (.D(multiplexer_5_out), .Q(_16_out), .clk(clk), .clr(areset));  // open: en
  and and_5 (and_5_out, _16_writer, writeEnable);
  Multiplexer #(.width(32)) multiplexer_6 (
    .in0(_17_out), .in1(writeData), .out(multiplexer_6_out), .sel(and_6_out));  // open: en
  Register #(.width(32)) register_6 (.D(multiplexer_6_out), .Q(_17_out), .clk(clk), .clr(areset));  // open: en
  and and_6 (and_6_out, _17_writer, writeEnable);
  Register #(.width(32)) register_7 (.D(multiplexer_7_out), .Q(_18_out), .clk(clk), .clr(areset));  // open: en
  Multiplexer #(.width(32)) multiplexer_7 (
    .in0(_18_out), .in1(writeData), .out(multiplexer_7_out), .sel(and_7_out));  // open: en
  and and_7 (and_7_out, _18_writer, writeEnable);
  Multiplexer #(.width(32)) multiplexer_8 (
    .in0(_19_out), .in1(writeData), .out(multiplexer_8_out), .sel(and_8_out));  // open: en
  Register #(.width(32)) register_8 (.D(multiplexer_8_out), .Q(_19_out), .clk(clk), .clr(areset));  // open: en
  and and_8 (and_8_out, _19_writer, writeEnable);
  Multiplexer #(.width(32)) multiplexer_9 (
    .in0(_4_out), .in1(writeData), .out(multiplexer_9_out), .sel(and_9_out));  // open: en
  and and_9 (and_9_out, _4_writer, writeEnable);
  Multiplexer #(.width(32)) multiplexer_10 (
    .in0(_5_out), .in1(writeData), .out(multiplexer_10_out), .sel(and_10_out));  // open: en
  and and_10 (and_10_out, _5_writer, writeEnable);
  Multiplexer #(.width(32)) multiplexer_11 (
    .in0(_6_out), .in1(writeData), .out(multiplexer_11_out), .sel(and_11_out));  // open: en
  and and_11 (and_11_out, _6_writer, writeEnable);
  Multiplexer #(.width(32)) multiplexer_12 (
    .in0(_7_out), .in1(writeData), .out(multiplexer_12_out), .sel(and_12_out));  // open: en
  and and_12 (and_12_out, _7_writer, writeEnable);
  Multiplexer #(.width(32)) multiplexer_13 (
    .in0(_20_out), .in1(writeData), .out(multiplexer_13_out), .sel(and_13_out));  // open: en
  and and_13 (and_13_out, _20_writer, writeEnable);
  Multiplexer #(.width(32)) multiplexer_14 (
    .in0(_21_out), .in1(writeData), .out(multiplexer_14_out), .sel(and_14_out));  // open: en
  and and_14 (and_14_out, _21_writer, writeEnable);
  Multiplexer #(.width(32)) multiplexer_15 (
    .in0(_22_out), .in1(writeData), .out(multiplexer_15_out), .sel(and_15_out));  // open: en
  and and_15 (and_15_out, _22_writer, writeEnable);
  Multiplexer #(.width(32)) multiplexer_16 (
    .in0(_23_out), .in1(writeData), .out(multiplexer_16_out), .sel(and_16_out));  // open: en
  and and_16 (and_16_out, _23_writer, writeEnable);
  Register #(.width(32)) register_9 (.D(multiplexer_9_out), .Q(_4_out), .clk(clk), .clr(areset));  // open: en
  Register #(.width(32)) register_10 (.D(multiplexer_10_out), .Q(_5_out), .clk(clk), .clr(areset));  // open: en
  Register #(.width(32)) register_11 (.D(multiplexer_11_out), .Q(_6_out), .clk(clk), .clr(areset));  // open: en
  Register #(.width(32)) register_12 (.D(multiplexer_12_out), .Q(_7_out), .clk(clk), .clr(areset));  // open: en
  Register #(.width(32)) register_13 (.D(multiplexer_13_out), .Q(_20_out), .clk(clk), .clr(areset));  // open: en
  Register #(.width(32)) register_14 (.D(multiplexer_14_out), .Q(_21_out), .clk(clk), .clr(areset));  // open: en
  Register #(.width(32)) register_15 (.D(multiplexer_15_out), .Q(_22_out), .clk(clk), .clr(areset));  // open: en
  Register #(.width(32)) register_16 (.D(multiplexer_16_out), .Q(_23_out), .clk(clk), .clr(areset));  // open: en
  Multiplexer #(.width(32)) multiplexer_17 (
    .in0(_8_out), .in1(writeData), .out(multiplexer_17_out), .sel(and_17_out));  // open: en
  and and_17 (and_17_out, _8_writer, writeEnable);
  Multiplexer #(.width(32)) multiplexer_18 (
    .in0(_9_out), .in1(writeData), .out(multiplexer_18_out), .sel(and_18_out));  // open: en
  and and_18 (and_18_out, _9_writer, writeEnable);
  Multiplexer #(.width(32)) multiplexer_19 (
    .in0(_10_out), .in1(writeData), .out(multiplexer_19_out), .sel(and_19_out));  // open: en
  and and_19 (and_19_out, _10_writer, writeEnable);
  Multiplexer #(.width(32)) multiplexer_20 (
    .in0(_11_out), .in1(writeData), .out(multiplexer_20_out), .sel(and_20_out));  // open: en
  and and_20 (and_20_out, _11_writer, writeEnable);
  Multiplexer #(.width(32)) multiplexer_21 (
    .in0(_24_out), .in1(writeData), .out(multiplexer_21_out), .sel(and_21_out));  // open: en
  Register #(.width(32)) register_17 (.D(multiplexer_21_out), .Q(_24_out), .clk(clk), .clr(areset));  // open: en
  and and_21 (and_21_out, _24_writer, writeEnable);
  Multiplexer #(.width(32)) multiplexer_22 (
    .in0(_25_out), .in1(writeData), .out(multiplexer_22_out), .sel(and_22_out));  // open: en
  Register #(.width(32)) register_18 (.D(multiplexer_22_out), .Q(_25_out), .clk(clk), .clr(areset));  // open: en
  and and_22 (and_22_out, _25_writer, writeEnable);
  Multiplexer #(.width(32)) multiplexer_23 (
    .in0(_26_out), .in1(writeData), .out(multiplexer_23_out), .sel(and_23_out));  // open: en
  Register #(.width(32)) register_19 (.D(multiplexer_23_out), .Q(_26_out), .clk(clk), .clr(areset));  // open: en
  and and_23 (and_23_out, _26_writer, writeEnable);
  Multiplexer #(.width(32)) multiplexer_24 (
    .in0(_27_out), .in1(writeData), .out(multiplexer_24_out), .sel(and_24_out));  // open: en
  Register #(.width(32)) register_20 (.D(multiplexer_24_out), .Q(_27_out), .clk(clk), .clr(areset));  // open: en
  and and_24 (and_24_out, _27_writer, writeEnable);
  Decoder #(.select(5)) decoder_1 (
    .out0(_0_writer), .out1(_1_writer), .out2(_2_writer), .out3(_3_writer), .out4(_4_writer),
    .out5(_5_writer), .out6(_6_writer), .out7(_7_writer), .out8(_8_writer), .out9(_9_writer),
    .out10(_10_writer), .out11(_11_writer), .out12(_12_writer), .out13(_13_writer), .out14(_14_writer),
    .out15(_15_writer), .out16(_16_writer), .out17(_17_writer), .out18(_18_writer), .out19(_19_writer),
    .out20(_20_writer), .out21(_21_writer), .out22(_22_writer), .out23(_23_writer), .out24(_24_writer),
    .out25(_25_writer), .out26(_26_writer), .out27(_27_writer), .out28(_28_writer), .out29(_29_writer),
    .out30(_30_writer), .out31(_31_writer), .sel(writeReg));  // open: en
  Register #(.width(32)) register_21 (.D(multiplexer_17_out), .Q(_8_out), .clk(clk), .clr(areset));  // open: en
  Register #(.width(32)) register_22 (.D(multiplexer_18_out), .Q(_9_out), .clk(clk), .clr(areset));  // open: en
  Register #(.width(32)) register_23 (.D(multiplexer_19_out), .Q(_10_out), .clk(clk), .clr(areset));  // open: en
  Register #(.width(32)) register_24 (.D(multiplexer_20_out), .Q(_11_out), .clk(clk), .clr(areset));  // open: en
  Multiplexer #(.select(5), .width(32)) multiplexer_25 (
    .in0(_0_out), .in1(_1_out), .in2(_2_out), .in3(_3_out), .in4(_4_out), .in5(_5_out), .in6(_6_out),
    .in7(_7_out), .in8(_8_out), .in9(_9_out), .in10(_10_out), .in11(_11_out), .in12(_12_out), .in13(_13_out),
    .in14(_14_out), .in15(_15_out), .in16(_16_out), .in17(_17_out), .in18(_18_out), .in19(_19_out),
    .in20(_20_out), .in21(_21_out), .in22(_22_out), .in23(_23_out), .in24(_24_out), .in25(_25_out),
    .in26(_26_out), .in27(_27_out), .in28(_28_out), .in29(_29_out), .in30(_30_out), .in31(_31_out),
    .out(regData1), .sel(readReg1));  // open: en
  Multiplexer #(.select(5), .width(32)) multiplexer_26 (
    .in0(_0_out), .in1(_1_out), .in2(_2_out), .in3(_3_out), .in4(_4_out), .in5(_5_out), .in6(_6_out),
    .in7(_7_out), .in8(_8_out), .in9(_9_out), .in10(_10_out), .in11(_11_out), .in12(_12_out), .in13(_13_out),
    .in14(_14_out), .in15(_15_out), .in16(_16_out), .in17(_17_out), .in18(_18_out), .in19(_19_out),
    .in20(_20_out), .in21(_21_out), .in22(_22_out), .in23(_23_out), .in24(_24_out), .in25(_25_out),
    .in26(_26_out), .in27(_27_out), .in28(_28_out), .in29(_29_out), .in30(_30_out), .in31(_31_out),
    .out(regData2), .sel(readReg2));  // open: en
  Register #(.width(32)) register_25 (.D(multiplexer_27_out), .Q(_12_out), .clk(clk), .clr(areset));  // open: en
  Multiplexer #(.width(32)) multiplexer_27 (
    .in0(_12_out), .in1(writeData), .out(multiplexer_27_out), .sel(and_25_out));  // open: en
  and and_25 (and_25_out, _12_writer, writeEnable);
  Multiplexer #(.width(32)) multiplexer_28 (
    .in0(_13_out), .in1(writeData), .out(multiplexer_28_out), .sel(and_26_out));  // open: en
  Register #(.width(32)) register_26 (.D(multiplexer_28_out), .Q(_13_out), .clk(clk), .clr(areset));  // open: en
  and and_26 (and_26_out, _13_writer, writeEnable);
  Register #(.width(32)) register_27 (.D(multiplexer_29_out), .Q(_14_out), .clk(clk), .clr(areset));  // open: en
  Multiplexer #(.width(32)) multiplexer_29 (
    .in0(_14_out), .in1(writeData), .out(multiplexer_29_out), .sel(and_27_out));  // open: en
  and and_27 (and_27_out, _14_writer, writeEnable);
  Multiplexer #(.width(32)) multiplexer_30 (
    .in0(_15_out), .in1(writeData), .out(multiplexer_30_out), .sel(and_28_out));  // open: en
  Register #(.width(32)) register_28 (.D(multiplexer_30_out), .Q(_15_out), .clk(clk), .clr(areset));  // open: en
  and and_28 (and_28_out, _15_writer, writeEnable);
  Multiplexer #(.width(32)) multiplexer_31 (
    .in0(_28_out), .in1(writeData), .out(multiplexer_31_out), .sel(and_29_out));  // open: en
  Register #(.width(32)) register_29 (.D(multiplexer_31_out), .Q(_28_out), .clk(clk), .clr(areset));  // open: en
  and and_29 (and_29_out, _28_writer, writeEnable);
  Register #(.width(32)) register_30 (.D(multiplexer_32_out), .Q(_29_out), .clk(clk), .clr(areset));  // open: en
  Multiplexer #(.width(32)) multiplexer_32 (
    .in0(_29_out), .in1(writeData), .out(multiplexer_32_out), .sel(and_30_out));  // open: en
  and and_30 (and_30_out, _29_writer, writeEnable);
  Register #(.width(32)) register_31 (.D(multiplexer_33_out), .Q(_30_out), .clk(clk), .clr(areset));  // open: en
  Multiplexer #(.width(32)) multiplexer_33 (
    .in0(_30_out), .in1(writeData), .out(multiplexer_33_out), .sel(and_31_out));  // open: en
  and and_31 (and_31_out, _30_writer, writeEnable);
  Multiplexer #(.width(32)) multiplexer_34 (
    .in0(_31_out), .in1(writeData), .out(multiplexer_34_out), .sel(and_32_out));  // open: en
  Register #(.width(32)) register_32 (.D(multiplexer_34_out), .Q(_31_out), .clk(clk), .clr(areset));  // open: en
  and and_32 (and_32_out, _31_writer, writeEnable);

  // Other names for the same wires on the sheet: clear = areset; in[31:0] = writeData; WE = writeEnable
endmodule

module IFU (
  input  clk,
  input  areset,
  input  [31:0] relativeAddr,
  input  condition,
  input  [25:0] jumpAddr,
  input  jump,
  output [31:0] instruction,
  output [31:0] PC
);

  wire [31:0] ifu_next_1_nextpc, shifter_1_out;

  Shifter #(.width(32)) shifter_1 (.in(relativeAddr), .\dist (5'b00010), .out(shifter_1_out));
  IFU_next ifu_next_1 (
    .previousPC(PC), .relativeAddr(shifter_1_out), .condition(condition), .nextPC(ifu_next_1_nextpc),
    .jumpAddr(jumpAddr), .jump(jump));
  Register #(.width(32)) register_1 (.D(ifu_next_1_nextpc), .Q(PC), .clk(clk), .clr(areset));  // open: en
  ROM #(.addrWidth(5), .dataWidth(32)) rom_1 (.addr(PC[6:2]), .data(instruction));  // open: sel

  // Notes on the sheet:
  //   contents of rom_1 (hex, n*v repeats v):
  //   40001ac
endmodule

module IFU_next (
  input  [31:0] previousPC,
  input  [31:0] relativeAddr,
  input  condition,
  input  [25:0] jumpAddr,
  input  jump,
  output [31:0] nextPC
);

  wire [31:0] adder_1_out, adder_2_out, multiplexer_1_out;

  Adder #(.width(32)) adder_1 (.a(previousPC), .b(32'h4), .out(adder_1_out));  // open: cin, cout
  Adder #(.width(32)) adder_2 (.a(adder_1_out), .b(relativeAddr), .out(adder_2_out));  // open: cin, cout
  Multiplexer #(.width(32)) multiplexer_1 (
    .in0(adder_1_out), .in1(adder_2_out), .out(multiplexer_1_out), .sel(condition));  // open: en
  Multiplexer #(.width(32)) multiplexer_2 (
    .in0(multiplexer_1_out), .in1({adder_1_out[31:28], jumpAddr, adder_1_out[1:0]}), .out(nextPC), .sel(jump));  // open: en
endmodule

module ALU (
  input  [31:0] data1,
  input  [31:0] data2,
  input  [2:0] operation,
  output equal,
  output [31:0] result
);

  wire [31:0] adder_1_out, or_1_out, shifter_1_out, subtractor_1_out;

  Adder #(.width(32)) adder_1 (.a(data1), .b(data2), .out(adder_1_out));  // open: cin, cout
  Subtractor #(.width(32)) subtractor_1 (.a(data1), .b(data2), .out(subtractor_1_out));  // open: bin, bout
  assign or_1_out = data1 | data2;  // OR_Gate or_1, 32 bits wide
  Shifter #(.width(32)) shifter_1 (.in(data2), .\dist (5'b10000), .out(shifter_1_out));
  Multiplexer #(.select(3), .width(32)) multiplexer_1 (
    .in0(adder_1_out), .in1(subtractor_1_out), .in2(or_1_out), .in3(shifter_1_out), .out(result),
    .sel(operation));  // open: in4, in5, in6, in7, en
  Comparator #(.width(32), .mode("unsigned")) comparator_1 (
    .a(subtractor_1_out), .b({32{1'b0}}), .eq(equal));  // open: gt, lt
endmodule

module InstructionSpliter (
  input  [31:0] instruction,
  output [25:0] jumpAddr,
  output [15:0] imm,
  output [5:0] funct,
  output [4:0] shamt,
  output [4:0] rd,
  output [4:0] rt,
  output [4:0] rs_base,
  output [5:0] opCode
);


  assign funct = instruction[5:0];
  assign imm = instruction[15:0];
  assign jumpAddr = instruction[25:0];
  assign opCode = instruction[31:26];
  assign rd = instruction[15:11];
  assign rs_base = instruction[25:21];
  assign rt = instruction[20:16];
  assign shamt = instruction[10:6];
endmodule

module Controller (
  input  [5:0] opCode,
  output writeRegSel,
  output writeRegDataSel,
  output aluData2Sel,
  output branch,
  output GRFwriteEnable,
  output DMwriteEnable,
  output DMreadEnable,
  output hasFunct,
  output [2:0] ALUvector,
  output zero_signEXT,
  output jump
);

  wire controller_andlogic_1_beq, controller_andlogic_1_j, controller_andlogic_1_lui,
       controller_andlogic_1_lw, controller_andlogic_1_ori, controller_andlogic_1_r_type,
       controller_andlogic_1_sw;

  Controller_andLogic controller_andlogic_1 (
    .in_1(opCode), .R_type(controller_andlogic_1_r_type), .ori(controller_andlogic_1_ori),
    .lw(controller_andlogic_1_lw), .sw(controller_andlogic_1_sw), .beq(controller_andlogic_1_beq),
    .lui(controller_andlogic_1_lui), .j(controller_andlogic_1_j));
  Controller_orLogic controller_orlogic_1 (
    .R_type(controller_andlogic_1_r_type), .ori(controller_andlogic_1_ori), .lw(controller_andlogic_1_lw),
    .sw(controller_andlogic_1_sw), .beq(controller_andlogic_1_beq), .writeRegRD_RT(writeRegSel),
    .writeRegDataALU_DM(writeRegDataSel), .aluData2REG_IMM(aluData2Sel), .equalBranch(branch),
    .GRFwriteEnable(GRFwriteEnable), .DMwriteEnable(DMwriteEnable), .DMreadEnable(DMreadEnable),
    .hasFunct(hasFunct), .ALUvector0(ALUvector[0]), .ALUvector1(ALUvector[1]), .ALUvector2(ALUvector[2]),
    .lui(controller_andlogic_1_lui), .zero_signEXT(zero_signEXT), .j(controller_andlogic_1_j), .jump(jump));
endmodule

module Controller_andLogic (
  input  [5:0] in_1,
  output R_type,
  output ori,
  output lw,
  output sw,
  output beq,
  output lui,
  output j
);

  wire not_1_out, not_2_out, not_3_out, not_4_out, not_5_out, not_6_out;

  not not_1 (not_1_out, in_1[5]);
  not not_2 (not_2_out, in_1[4]);
  not not_3 (not_3_out, in_1[3]);
  not not_4 (not_4_out, in_1[0]);
  not not_5 (not_5_out, in_1[1]);
  not not_6 (not_6_out, in_1[2]);
  and and_1 (R_type, not_1_out, not_2_out, not_3_out, not_6_out, not_5_out, not_4_out);
  and and_2 (ori, not_1_out, not_2_out, in_1[3], in_1[2], not_5_out, in_1[0]);
  and and_3 (lw, in_1[5], not_2_out, not_3_out, not_6_out, in_1[1], in_1[0]);
  and and_4 (sw, in_1[5], not_2_out, in_1[3], not_6_out, in_1[1], in_1[0]);
  and and_5 (beq, not_1_out, not_2_out, not_3_out, in_1[2], not_5_out, not_4_out);
  and and_6 (lui, not_1_out, not_2_out, in_1[3], in_1[2], in_1[1], in_1[0]);
  and and_7 (j, not_1_out, not_2_out, not_3_out, not_6_out, in_1[1], not_4_out);
endmodule

module Controller_orLogic (
  input  R_type,
  input  ori,
  input  lw,
  input  sw,
  input  beq,
  input  lui,
  input  j,
  output writeRegRD_RT,
  output writeRegDataALU_DM,
  output aluData2REG_IMM,
  output equalBranch,
  output GRFwriteEnable,
  output DMwriteEnable,
  output DMreadEnable,
  output hasFunct,
  output ALUvector0,
  output ALUvector1,
  output ALUvector2,
  output zero_signEXT,
  output jump
);

  or or_1 (writeRegRD_RT, ori, lw, lui);
  buf or_2 (writeRegDataALU_DM, lw);  // OR_Gate
  or or_3 (aluData2REG_IMM, ori, lw, sw, lui);
  buf or_4 (equalBranch, beq);  // OR_Gate
  or or_5 (GRFwriteEnable, R_type, ori, lw, lui);
  buf or_6 (DMwriteEnable, sw);  // OR_Gate
  buf or_7 (DMreadEnable, lw);  // OR_Gate
  buf or_8 (hasFunct, R_type);  // OR_Gate
  or or_9 (ALUvector0, lui, 1'b0);
  or or_10 (ALUvector1, ori, lui, 1'b0);
  buf or_11 (ALUvector2, 1'b0);  // OR_Gate
  or or_12 (zero_signEXT, lw, sw, beq);
  buf or_13 (jump, j);  // OR_Gate
endmodule

module ALUController (
  input  hasFunct,
  input  [2:0] ALUvector,
  input  [5:0] funct,
  output [2:0] ALUOp
);

  wire and_1_out, and_2_out, not_1_out, not_2_out, not_3_out, not_4_out, not_5_out, not_6_out;
  wire [2:0] or_1_out;

  not not_1 (not_1_out, funct[5]);
  not not_2 (not_2_out, funct[4]);
  not not_3 (not_3_out, funct[3]);
  not not_4 (not_4_out, funct[0]);
  not not_5 (not_5_out, funct[2]);
  not not_6 (not_6_out, funct[1]);
  and and_1 (and_1_out, funct[5], not_2_out, not_3_out, not_5_out, not_6_out, funct[0]);
  and and_2 (and_2_out, funct[5], not_2_out, not_3_out, not_5_out, funct[1], funct[0]);
  or or_1 (or_1_out[0], and_2_out, 1'b0);
  buf or_2 (or_1_out[1], 1'b0);  // OR_Gate
  buf or_3 (or_1_out[2], 1'b0);  // OR_Gate
  Multiplexer #(.width(3)) multiplexer_1 (.in0(ALUvector), .in1(or_1_out), .out(ALUOp), .sel(hasFunct));  // open: en

  // Notes on the sheet:
  //   addu
  //   subu
  //   alu0
  //   alu1
  //   alu2
endmodule

module BranchController (
  input  equal,
  input  branchEqual,
  output condition
);

  wire and_1_out;

  and and_1 (and_1_out, equal, branchEqual);
  buf or_1 (condition, and_1_out);  // OR_Gate
endmodule
