// Logisim project P3 new.circ as structural Verilog: 9 circuits, main circuit main
module main (
  input  areset,
  output [31:0] instruction,
  output RegWrite,
  output [4:0] RegAddr,
  output [31:0] RegData,
  output MemWrite,
  output [4:0] MemAddr,
  output [31:0] MemData
);

  wire branch, clock_1_out, controller_1_isr, controller_1_zero, controller_and_1_beq, controller_and_1_bgez,
       controller_and_1_j, controller_and_1_lui, controller_and_1_lw, controller_and_1_ori,
       controller_and_1_r_type, controller_and_1_sw, DM_ALU, DMRE, imm_rt, jump, rt_rdIN, zero, zero_signEXT;
  wire [1:0] bit_extender_4_out;
  wire [2:0] ALUOp, compToZero, controller_1_alu0, controller_1_cmp0;
  wire [4:0] instructionspliter_1_rd, instructionspliter_1_rs_base, instructionspliter_1_rt;
  wire [5:0] instructionspliter_1_funct, instructionspliter_1_opcode;
  wire [6:0] bit_extender_1_out;
  wire [15:0] instructionspliter_1_imm;
  wire [25:0] instructionspliter_1_jumpaddr;
  wire [31:0] adder_1_out, adder_2_out, alu_1_result, bit_extender_2_out, bit_extender_3_out, grf_1_regdata1,
       multiplexer_1_out, multiplexer_2_out, multiplexer_3_out, multiplexer_5_out, PC_q, ram_1_data,
       shifter_1_out;

  Clock clock_1 (.out(clock_1_out));
  controller_and controller_and_1 (
    .in_1(instructionspliter_1_opcode), .R_type(controller_and_1_r_type), .ori(controller_and_1_ori),
    .lw(controller_and_1_lw), .sw(controller_and_1_sw), .beq(controller_and_1_beq),
    .lui(controller_and_1_lui), .j(controller_and_1_j), .bgez(controller_and_1_bgez));
  controller controller_1 (
    .opCode(instructionspliter_1_opcode), .jump(jump), .zero_sign(zero_signEXT), .rt_rdIn(rt_rdIN),
    .imm_rt(imm_rt), .DM_ALU(DM_ALU), .GRFWE(RegWrite), .DMRE(DMRE), .DMWE(MemWrite),
    .alu0(controller_1_alu0[0]), .alu1(controller_1_alu0[1]), .alu2(controller_1_alu0[2]),
    .cmp0(controller_1_cmp0[0]), .cmp1(controller_1_cmp0[1]), .cmp2(controller_1_cmp0[2]),
    .zero(controller_1_zero), .isR(controller_1_isr));
  Register #(.width(32)) PC (.D(multiplexer_2_out), .Q(PC_q), .clk(clock_1_out), .clr(areset));  // open: en
  ALUcontrol alucontrol_1 (
    .aluOP(controller_1_alu0), .isR(controller_1_isr), .funct(instructionspliter_1_funct), .opCode(ALUOp));
  Adder #(.width(32)) adder_1 (.a(32'h4), .b(PC_q), .out(adder_1_out));  // open: cin, cout
  Shifter #(.width(32)) shifter_1 (.in(multiplexer_3_out), .\dist (5'b00010), .out(shifter_1_out));
  Bit_Extender #(.in_width(32), .out_width(7)) bit_extender_1 (.in(PC_q), .out(bit_extender_1_out));
  BranchControl branchcontrol_1 (
    .zero(zero), .branchZero(controller_1_zero), .comp(compToZero), .BranchComp(controller_1_cmp0),
    .branch(branch), .rt(instructionspliter_1_rt));
  Adder #(.width(32)) adder_2 (.a(adder_1_out), .b(shifter_1_out), .out(adder_2_out));  // open: cin, cout
  Multiplexer #(.width(32)) multiplexer_1 (
    .in0(adder_1_out), .in1(adder_2_out), .out(multiplexer_1_out), .sel(branch));  // open: en
  ROM #(.addrWidth(5), .dataWidth(32)) rom_1 (.addr(bit_extender_1_out[6:2]), .data(instruction));  // open: sel
  InstructionSpliter instructionspliter_1 (
    .instruction(instruction), .imm(instructionspliter_1_imm), .funct(instructionspliter_1_funct),
    .rd(instructionspliter_1_rd), .rt(instructionspliter_1_rt), .rs_base(instructionspliter_1_rs_base),
    .opCode(instructionspliter_1_opcode), .jumpAddr(instructionspliter_1_jumpaddr));  // open: shamt
  assign bit_extender_2_out = {{16{1'b0}}, instructionspliter_1_imm};  // Bit_Extender bit_extender_2
  assign bit_extender_3_out = {{16{instructionspliter_1_imm[15]}}, instructionspliter_1_imm};  // Bit_Extender bit_extender_3
  Multiplexer #(.width(32)) multiplexer_2 (
    .in0(multiplexer_1_out),
    .in1({multiplexer_1_out[31:28], instructionspliter_1_jumpaddr, multiplexer_1_out[1:0]}),
    .out(multiplexer_2_out), .sel(jump));  // open: en
  Multiplexer #(.width(32)) multiplexer_3 (
    .in0(bit_extender_2_out), .in1(bit_extender_3_out), .out(multiplexer_3_out), .sel(zero_signEXT));  // open: en
  Multiplexer #(.width(5)) multiplexer_4 (
    .in0(instructionspliter_1_rt), .in1(instructionspliter_1_rd), .out(RegAddr), .sel(rt_rdIN));  // open: en
  GRF grf_1 (
    .readReg1(instructionspliter_1_rs_base), .readReg2(instructionspliter_1_rt), .writeReg(RegAddr),
    .writeData(RegData), .regData1(grf_1_regdata1), .regData2(MemData), .clk(clock_1_out), .areset(areset),
    .writeEnable(RegWrite));
  Multiplexer #(.width(32)) multiplexer_5 (
    .in0(multiplexer_3_out), .in1(MemData), .out(multiplexer_5_out), .sel(imm_rt));  // open: en
  ALU alu_1 (
    .data1(grf_1_regdata1), .data2(multiplexer_5_out), .comp(compToZero), .result(alu_1_result),
    .operation(ALUOp), .zero(zero));  // open: shamt
  // Probe on alu_1_result
  Bit_Extender #(.in_width(32), .out_width(7)) bit_extender_4 (.in(alu_1_result), .out({MemAddr, bit_extender_4_out}));
  RAM #(.addrWidth(5), .dataWidth(32), .bus("separate")) ram_1 (
    .addr(MemAddr), .din(MemData), .data(ram_1_data), .str(MemWrite), .clk(clock_1_out), .ld(DMRE),
    .clr(areset));  // open: sel
  Multiplexer #(.width(32)) multiplexer_6 (
    .in0(ram_1_data), .in1(alu_1_result), .out(RegData), .sel(DM_ALU));  // open: en

  // Other names for the same wires on the sheet: DMWE = MemWrite; GRF_WE = RegWrite

  // Notes on the sheet:
  //   R
  //   ori
  //   lw
  //   sw
  //   beq
  //   lui
  //   j
  //   bgez
  //   contents of rom_1 (hex, n*v repeats v):
  //   37390000 34080001 3409ffff ac080000 0 3c0affff af2a0004 354affff af2a0008 0 8f2b0008 8c0c0000
  //   16c6821 af2d000c 16b7021 af2e0010 1087821 af2f0014 0 8f300014 8f310010 2119023 af320018 0 36730003
  //   12600003 2689823 8000c19 0 af33001c
endmodule

module InstructionSpliter (
  input  [31:0] instruction,
  output [25:0] jumpAddr,
  output [15:0] imm,
  output [5:0] funct,
  output [4:0] shamt,
  output [4:0] rd,
  output [4:0] rt,
  output [4:0] rs_base,
  output [5:0] opCode
);


  assign funct = instruction[5:0];
  assign imm = instruction[15:0];
  assign jumpAddr = instruction[25:0];
  assign opCode = instruction[31:26];
  assign rd = instruction[15:11];
  assign rs_base = instruction[25:21];
  assign rt = instruction[20:16];
  assign shamt = instruction[10:6];
endmodule

module GRF (
  input  clk,
  input  areset,
  input  writeEnable,
  input  [4:0] readReg1,
  input  [4:0] readReg2,
  input  [4:0] writeReg,
  input  [31:0] writeData,
  output [31:0] regData1,
  output [31:0] regData2
);

  wire _0_writer, _1_writer, _2_writer, _3_writer, _4_writer, _5_writer, _6_writer, _7_writer, _8_writer,
       _9_writer, _10_writer, _11_writer, _12_writer, _13_writer, _14_writer, _15_writer, _16_writer,
       _17_writer, _18_writer, _19_writer, _20_writer, _21_writer, _22_writer, _23_writer, _24_writer,
       _25_writer, _26_writer, _27_writer, _28_writer, _29_writer, _30_writer, _31_writer, and_1_out,
       and_2_out, and_3_out, and_4_out, and_5_out, and_6_out, and_7_out, and_8_out, and_9_out, and_10_out,
       and_11_out, and_12_out, and_13_out, and_14_out, and_15_out, and_16_out, and_17_out, and_18_out,
       and_19_out, and_20_out, and_21_out, and_22_out, and_23_out, and_24_out, and_25_out, and_26_out,
       and_27_out, and_28_out, and_29_out, and_30_out, and_31_out, and_32_out;
  wire [31:0] _0_out, _1_out, _2_out, _3_out, _4_out, _5_out, _6_out, _7_out, _8_out, _9_out, _10_out,
       _11_out, _12_out, _13_out, _14_out, _15_out, _16_out, _17_out, _18_out, _19_out, _20_out, _21_out,
       _22_out, _23_out, _24_out, _25_out, _26_out, _27_out, _28_out, _29_out, _30_out, _31_out,
       multiplexer_1_out, multiplexer_2_out, multiplexer_3_out, multiplexer_4_out, multiplexer_5_out,
       multiplexer_6_out, multiplexer_7_out, multiplexer_8_out, multiplexer_9_out, multiplexer_10_out,
       multiplexer_11_out, multiplexer_12_out, multiplexer_13_out, multiplexer_14_out, multiplexer_15_out,
       multiplexer_16_out, multiplexer_17_out, multiplexer_18_out, multiplexer_19_out, multiplexer_20_out,
       multiplexer_21_out, multiplexer_22_out, multiplexer_23_out, multiplexer_24_out, multiplexer_27_out,
       multiplexer_28_out, multiplexer_29_out, multiplexer_30_out, multiplexer_31_out, multiplexer_32_out,
       multiplexer_33_out, multiplexer_34_out;

  Multiplexer #(.width(32)) multiplexer_1 (
    .in0(_0_out), .in1(writeData), .out(multiplexer_1_out), .sel(and_1_out));  // open: en
  Register #(.width(32)) register_1 (.D(multiplexer_1_out), .Q(_0_out), .clk(clk), .clr(1'b1));  // open: en
  and and_1 (and_1_out, _0_writer, writeEnable);
  Multiplexer #(.width(32)) multiplexer_2 (
    .in0(_1_out), .in1(writeData), .out(multiplexer_2_out), .sel(and_2_out));  // open: en
  Register #(.width(32)) register_2 (.D(multiplexer_2_out), .Q(_1_out), .clk(clk), .clr(areset));  // open: en
  and and_2 (and_2_out, _1_writer, writeEnable);
  Multiplexer #(.width(32)) multiplexer_3 (
    .in0(_2_out), .in1(writeData), .out(multiplexer_3_out), .sel(and_3_out));  // open: en
  Register #(.width(32)) register_3 (.D(multiplexer_3_out), .Q(_2_out), .clk(clk), .clr(areset));  // open: en
  and and_3 (and_3_out, _2_writer, writeEnable);
  Multiplexer #(.width(32)) multiplexer_4 (
    .in0(_3_out), .in1(writeData), .out(multiplexer_4_out), .sel(and_4_out));  // open: en
  Register #(.width(32)) register_4 (.D(multiplexer_4_out), .Q(_3_out), .clk(clk), .clr(areset));  // open: en
  and and_4 (and_4_out, _3_writer, writeEnable);
  Multiplexer #(.width(32)) multiplexer_5 (
    .in0(_16_out), .in1(writeData), .out(multiplexer_5_out), .sel(and_5_out));  // open: en
  Register #(.width(32)) register_5 (.D(multiplexer_5_out), .Q(_16_out), .clk(clk), .clr(areset));  // open: en
  and and_5 (and_5_out, _16_writer, writeEnable);
  Register #(.width(32)) register_6 (.D(multiplexer_6_out), .Q(_17_out), .clk(clk), .clr(areset));  // open: en
  Multiplexer #(.width(32)) multiplexer_6 (
    .in0(_17_out), .in1(writeData), .out(multiplexer_6_out), .sel(and_6_out));  // open: en
  and and_6 (and_6_out, _17_writer, writeEnable);
  Register #(.width(32)) register_7 (.D(multiplexer_7_out), .Q(_18_out), .clk(clk), .clr(areset));  // open: en
  Multiplexer #(.width(32)) multiplexer_7 (
    .in0(_18_out), .in1(writeData), .out(multiplexer_7_out), .sel(and_7_out));  // open: en
  and and_7 (and_7_out, _18_writer, writeEnable);
  Register #(.width(32)) register_8 (.D(multiplexer_8_out), .Q(_19_out), .clk(clk), .clr(areset));  // open: en
  Multiplexer #(.width(32)) multiplexer_8 (
    .in0(_19_out), .in1(writeData), .out(multiplexer_8_out), .sel(and_8_out));  // open: en
  and and_8 (and_8_out, _19_writer, writeEnable);
  Multiplexer #(.width(32)) multiplexer_9 (
    .in0(_4_out), .in1(writeData), .out(multiplexer_9_out), .sel(and_9_out));  // open: en
  and and_9 (and_9_out, _4_writer, writeEnable);
  Multiplexer #(.width(32)) multiplexer_10 (
    .in0(_5_out), .in1(writeData), .out(multiplexer_10_out), .sel(and_10_out));  // open: en
  and and_10 (and_10_out, _5_writer, writeEnable);
  Multiplexer #(.width(32)) multiplexer_11 (
    .in0(_6_out), .in1(writeData), .out(multiplexer_11_out), .sel(and_11_out));  // open: en
  and and_11 (and_11_out, _6_writer, writeEnable);
  Multiplexer #(.width(32)) multiplexer_12 (
    .in0(_7_out), .in1(writeData), .out(multiplexer_12_out), .sel(and_12_out));  // open: en
  and and_12 (and_12_out, _7_writer, writeEnable);
  Multiplexer #(.width(32)) multiplexer_13 (
    .in0(_20_out), .in1(writeData), .out(multiplexer_13_out), .sel(and_13_out));  // open: en
  and and_13 (and_13_out, _20_writer, writeEnable);
  Multiplexer #(.width(32)) multiplexer_14 (
    .in0(_21_out), .in1(writeData), .out(multiplexer_14_out), .sel(and_14_out));  // open: en
  and and_14 (and_14_out, _21_writer, writeEnable);
  Multiplexer #(.width(32)) multiplexer_15 (
    .in0(_22_out), .in1(writeData), .out(multiplexer_15_out), .sel(and_15_out));  // open: en
  and and_15 (and_15_out, _22_writer, writeEnable);
  Multiplexer #(.width(32)) multiplexer_16 (
    .in0(_23_out), .in1(writeData), .out(multiplexer_16_out), .sel(and_16_out));  // open: en
  and and_16 (and_16_out, _23_writer, writeEnable);
  Register #(.width(32)) register_9 (.D(multiplexer_9_out), .Q(_4_out), .clk(clk), .clr(areset));  // open: en
  Register #(.width(32)) register_10 (.D(multiplexer_10_out), .Q(_5_out), .clk(clk), .clr(areset));  // open: en
  Register #(.width(32)) register_11 (.D(multiplexer_11_out), .Q(_6_out), .clk(clk), .clr(areset));  // open: en
  Register #(.width(32)) register_12 (.D(multiplexer_12_out), .Q(_7_out), .clk(clk), .clr(areset));  // open: en
  Register #(.width(32)) register_13 (.D(multiplexer_13_out), .Q(_20_out), .clk(clk), .clr(areset));  // open: en
  Register #(.width(32)) register_14 (.D(multiplexer_14_out), .Q(_21_out), .clk(clk), .clr(areset));  // open: en
  Register #(.width(32)) register_15 (.D(multiplexer_15_out), .Q(_22_out), .clk(clk), .clr(areset));  // open: en
  Register #(.width(32)) register_16 (.D(multiplexer_16_out), .Q(_23_out), .clk(clk), .clr(areset));  // open: en
  Multiplexer #(.width(32)) multiplexer_17 (
    .in0(_8_out), .in1(writeData), .out(multiplexer_17_out), .sel(and_17_out));  // open: en
  and and_17 (and_17_out, _8_writer, writeEnable);
  Multiplexer #(.width(32)) multiplexer_18 (
    .in0(_9_out), .in1(writeData), .out(multiplexer_18_out), .sel(and_18_out));  // open: en
  and and_18 (and_18_out, _9_writer, writeEnable);
  Multiplexer #(.width(32)) multiplexer_19 (
    .in0(_10_out), .in1(writeData), .out(multiplexer_19_out), .sel(and_19_out));  // open: en
  and and_19 (and_19_out, _10_writer, writeEnable);
  Multiplexer #(.width(32)) multiplexer_20 (
    .in0(_11_out), .in1(writeData), .out(multiplexer_20_out), .sel(and_20_out));  // open: en
  and and_20 (and_20_out, _11_writer, writeEnable);
  Register #(.width(32)) register_17 (.D(multiplexer_21_out), .Q(_24_out), .clk(clk), .clr(areset));  // open: en
  Multiplexer #(.width(32)) multiplexer_21 (
    .in0(_24_out), .in1(writeData), .out(multiplexer_21_out), .sel(and_21_out));  // open: en
  and and_21 (and_21_out, _24_writer, writeEnable);
  Multiplexer #(.width(32)) multiplexer_22 (
    .in0(_25_out), .in1(writeData), .out(multiplexer_22_out), .sel(and_22_out));  // open: en
  Register #(.width(32)) register_18 (.D(multiplexer_22_out), .Q(_25_out), .clk(clk), .clr(areset));  // open: en
  and and_22 (and_22_out, _25_writer, writeEnable);
  Multiplexer #(.width(32)) multiplexer_23 (
    .in0(_26_out), .in1(writeData), .out(multiplexer_23_out), .sel(and_23_out));  // open: en
  Register #(.width(32)) register_19 (.D(multiplexer_23_out), .Q(_26_out), .clk(clk), .clr(areset));  // open: en
  and and_23 (and_23_out, _26_writer, writeEnable);
  Register #(.width(32)) register_20 (.D(multiplexer_24_out), .Q(_27_out), .clk(clk), .clr(areset));  // open: en
  Multiplexer #(.width(32)) multiplexer_24 (
    .in0(_27_out), .in1(writeData), .out(multiplexer_24_out), .sel(and_24_out));  // open: en
  and and_24 (and_24_out, _27_writer, writeEnable);
  Decoder #(.select(5)) decoder_1 (
    .out0(_0_writer), .out1(_1_writer), .out2(_2_writer), .out3(_3_writer), .out4(_4_writer),
    .out5(_5_writer), .out6(_6_writer), .out7(_7_writer), .out8(_8_writer), .out9(_9_writer),
    .out10(_10_writer), .out11(_11_writer), .out12(_12_writer), .out13(_13_writer), .out14(_14_writer),
    .out15(_15_writer), .out16(_16_writer), .out17(_17_writer), .out18(_18_writer), .out19(_19_writer),
    .out20(_20_writer), .out21(_21_writer), .out22(_22_writer), .out23(_23_writer), .out24(_24_writer),
    .out25(_25_writer), .out26(_26_writer), .out27(_27_writer), .out28(_28_writer), .out29(_29_writer),
    .out30(_30_writer), .out31(_31_writer), .sel(writeReg));  // open: en
  Register #(.width(32)) register_21 (.D(multiplexer_17_out), .Q(_8_out), .clk(clk), .clr(areset));  // open: en
  Register #(.width(32)) register_22 (.D(multiplexer_18_out), .Q(_9_out), .clk(clk), .clr(areset));  // open: en
  Register #(.width(32)) register_23 (.D(multiplexer_19_out), .Q(_10_out), .clk(clk), .clr(areset));  // open: en
  Register #(.width(32)) register_24 (.D(multiplexer_20_out), .Q(_11_out), .clk(clk), .clr(areset));  // open: en
  Multiplexer #(.select(5), .width(32)) multiplexer_25 (
    .in0(_0_out), .in1(_1_out), .in2(_2_out), .in3(_3_out), .in4(_4_out), .in5(_5_out), .in6(_6_out),
    .in7(_7_out), .in8(_8_out), .in9(_9_out), .in10(_10_out), .in11(_11_out), .in12(_12_out), .in13(_13_out),
    .in14(_14_out), .in15(_15_out), .in16(_16_out), .in17(_17_out), .in18(_18_out), .in19(_19_out),
    .in20(_20_out), .in21(_21_out), .in22(_22_out), .in23(_23_out), .in24(_24_out), .in25(_25_out),
    .in26(_26_out), .in27(_27_out), .in28(_28_out), .in29(_29_out), .in30(_30_out), .in31(_31_out),
    .out(regData1), .sel(readReg1));  // open: en
  Multiplexer #(.select(5), .width(32)) multiplexer_26 (
    .in0(_0_out), .in1(_1_out), .in2(_2_out), .in3(_3_out), .in4(_4_out), .in5(_5_out), .in6(_6_out),
    .in7(_7_out), .in8(_8_out), .in9(_9_out), .in10(_10_out), .in11(_11_out), .in12(_12_out), .in13(_13_out),
    .in14(_14_out), .in15(_15_out), .in16(_16_out), .in17(_17_out), .in18(_18_out), .in19(_19_out),
    .in20(_20_out), .in21(_21_out), .in22(_22_out), .in23(_23_out), .in24(_24_out), .in25(_25_out),
    .in26(_26_out), .in27(_27_out), .in28(_28_out), .in29(_29_out), .in30(_30_out), .in31(_31_out),
    .out(regData2), .sel(readReg2));  // open: en
  Multiplexer #(.width(32)) multiplexer_27 (
    .in0(_12_out), .in1(writeData), .out(multiplexer_27_out), .sel(and_25_out));  // open: en
  Register #(.width(32)) register_25 (.D(multiplexer_27_out), .Q(_12_out), .clk(clk), .clr(areset));  // open: en
  and and_25 (and_25_out, _12_writer, writeEnable);
  Register #(.width(32)) register_26 (.D(multiplexer_28_out), .Q(_13_out), .clk(clk), .clr(areset));  // open: en
  Multiplexer #(.width(32)) multiplexer_28 (
    .in0(_13_out), .in1(writeData), .out(multiplexer_28_out), .sel(and_26_out));  // open: en
  and and_26 (and_26_out, _13_writer, writeEnable);
  Multiplexer #(.width(32)) multiplexer_29 (
    .in0(_14_out), .in1(writeData), .out(multiplexer_29_out), .sel(and_27_out));  // open: en
  Register #(.width(32)) register_27 (.D(multiplexer_29_out), .Q(_14_out), .clk(clk), .clr(areset));  // open: en
  and and_27 (and_27_out, _14_writer, writeEnable);
  Multiplexer #(.width(32)) multiplexer_30 (
    .in0(_15_out), .in1(writeData), .out(multiplexer_30_out), .sel(and_28_out));  // open: en
  Register #(.width(32)) register_28 (.D(multiplexer_30_out), .Q(_15_out), .clk(clk), .clr(areset));  // open: en
  and and_28 (and_28_out, _15_writer, writeEnable);
  Register #(.width(32)) register_29 (.D(multiplexer_31_out), .Q(_28_out), .clk(clk), .clr(areset));  // open: en
  Multiplexer #(.width(32)) multiplexer_31 (
    .in0(_28_out), .in1(writeData), .out(multiplexer_31_out), .sel(and_29_out));  // open: en
  and and_29 (and_29_out, _28_writer, writeEnable);
  Register #(.width(32)) register_30 (.D(multiplexer_32_out), .Q(_29_out), .clk(clk), .clr(areset));  // open: en
  Multiplexer #(.width(32)) multiplexer_32 (
    .in0(_29_out), .in1(writeData), .out(multiplexer_32_out), .sel(and_30_out));  // open: en
  and and_30 (and_30_out, _29_writer, writeEnable);
  Register #(.width(32)) register_31 (.D(multiplexer_33_out), .Q(_30_out), .clk(clk), .clr(areset));  // open: en
  Multiplexer #(.width(32)) multiplexer_33 (
    .in0(_30_out), .in1(writeData), .out(multiplexer_33_out), .sel(and_31_out));  // open: en
  and and_31 (and_31_out, _30_writer, writeEnable);
  Register #(.width(32)) register_32 (.D(multiplexer_34_out), .Q(_31_out), .clk(clk), .clr(areset));  // open: en
  Multiplexer #(.width(32)) multiplexer_34 (
    .in0(_31_out), .in1(writeData), .out(multiplexer_34_out), .sel(and_32_out));  // open: en
  and and_32 (and_32_out, _31_writer, writeEnable);

  // Other names for the same wires on the sheet: clear = areset; in[31:0] = writeData; WE = writeEnable
endmodule

module ALU (
  input  [4:0] shamt,
  input  [31:0] data1,
  input  [31:0] data2,
  input  [2:0] operation,
  output [2:0] comp,
  output zero,
  output [31:0] result
);

  wire comparator_1_lt;
  wire [31:0] adder_1_out, multiplexer_1_out, or_1_out, shifter_1_out, subtractor_1_out;

  Adder #(.width(32)) adder_1 (.a(data1), .b(data2), .out(adder_1_out));  // open: cin, cout
  Subtractor #(.width(32)) subtractor_1 (.a(data1), .b(data2), .out(subtractor_1_out));  // open: bin, bout
  assign or_1_out = data1 | data2;  // OR_Gate or_1, 32 bits wide
  Shifter #(.width(32)) shifter_1 (.in(data2), .\dist (5'b10000), .out(shifter_1_out));
  Comparator #(.width(32)) comparator_1 (.a(data1), .b(data2), .lt(comparator_1_lt));  // open: gt, eq
  Multiplexer #(.width(32)) multiplexer_1 (
    .in0({32{1'b0}}), .in1(32'h1), .out(multiplexer_1_out), .sel(comparator_1_lt));  // open: en
  Comparator #(.width(32), .mode("unsigned")) comparator_2 (
    .a(data1), .b({32{1'b0}}), .gt(comp[2]), .eq(comp[1]), .lt(comp[0]));
  Comparator #(.width(32), .mode("unsigned")) comparator_3 (
    .a(subtractor_1_out), .b({32{1'b0}}), .eq(zero));  // open: gt, lt
  Multiplexer #(.select(3), .width(32)) multiplexer_2 (
    .in0(adder_1_out), .in1(subtractor_1_out), .in2(or_1_out), .in3(shifter_1_out), .in4(multiplexer_1_out),
    .out(result), .sel(operation));  // open: in5, in6, in7, en
endmodule

module controller (
  input  [5:0] opCode,
  output jump,
  output zero_sign,
  output rt_rdIn,
  output imm_rt,
  output DM_ALU,
  output GRFWE,
  output DMRE,
  output DMWE,
  output alu0,
  output alu1,
  output alu2,
  output cmp0,
  output cmp1,
  output cmp2,
  output zero,
  output isR
);

  wire controller_and_1_beq, controller_and_1_bgez, controller_and_1_j, controller_and_1_lui,
       controller_and_1_lw, controller_and_1_ori, controller_and_1_sw;

  controller_and controller_and_1 (
    .in_1(opCode), .R_type(isR), .ori(controller_and_1_ori), .lw(controller_and_1_lw),
    .sw(controller_and_1_sw), .beq(controller_and_1_beq), .lui(controller_and_1_lui), .j(controller_and_1_j),
    .bgez(controller_and_1_bgez));
  buf or_1 (jump, controller_and_1_j);  // OR_Gate
  or or_2 (zero_sign, controller_and_1_sw, controller_and_1_lw, controller_and_1_bgez);
  buf or_3 (rt_rdIn, isR);  // OR_Gate
  or or_4 (imm_rt, isR, controller_and_1_beq);
  or or_5 (DM_ALU, isR, controller_and_1_ori, controller_and_1_lui);
  or or_6 (GRFWE, isR, controller_and_1_ori, controller_and_1_lui, controller_and_1_lw);
  buf or_7 (DMRE, controller_and_1_lw);  // OR_Gate
  buf or_8 (DMWE, controller_and_1_sw);  // OR_Gate
  or or_9 (alu0, controller_and_1_lui, 1'b0);
  or or_10 (alu1, controller_and_1_ori, controller_and_1_lui, 1'b0);
  buf or_11 (alu2, 1'b0);  // OR_Gate
  buf or_12 (cmp0, 1'b0);  // OR_Gate
  or or_13 (cmp1, controller_and_1_bgez, 1'b0);
  or or_14 (cmp2, controller_and_1_bgez, 1'b0);
  or or_15 (zero, controller_and_1_beq, 1'b0);

  // Notes on the sheet:
  //   R
  //   ori
  //   lw
  //   sw
  //   beq
  //   lui
  //   j
  //   bgez
endmodule

module controller_and (
  input  [5:0] in_1,
  output R_type,
  output ori,
  output lw,
  output sw,
  output beq,
  output lui,
  output j,
  output bgez
);

  wire not_1_out, not_2_out, not_3_out, not_4_out, not_5_out, not_6_out;

  not not_1 (not_1_out, in_1[4]);
  not not_2 (not_2_out, in_1[5]);
  not not_3 (not_3_out, in_1[3]);
  not not_4 (not_4_out, in_1[0]);
  not not_5 (not_5_out, in_1[1]);
  not not_6 (not_6_out, in_1[2]);
  and and_1 (R_type, not_2_out, not_1_out, not_3_out, not_6_out, not_5_out, not_4_out);
  and and_2 (ori, not_2_out, not_1_out, in_1[3], in_1[2], not_5_out, in_1[0]);
  and and_3 (lw, in_1[5], not_1_out, not_3_out, not_6_out, in_1[1], in_1[0]);
  and and_4 (sw, in_1[5], not_1_out, in_1[3], not_6_out, in_1[1], in_1[0]);
  and and_5 (beq, not_2_out, not_1_out, not_3_out, in_1[2], not_5_out, not_4_out);
  and and_6 (lui, not_2_out, not_1_out, in_1[3], in_1[2], in_1[1], in_1[0]);
  and and_7 (j, not_2_out, not_1_out, not_3_out, not_6_out, in_1[1], not_4_out);
  and and_8 (bgez, not_2_out, not_1_out, not_3_out, not_6_out, not_5_out, in_1[0]);
endmodule

module ALUcontrol (
  input  [2:0] aluOP,
  input  isR,
  input  [5:0] funct,
  output [2:0] opCode
);

  wire and_1_out, and_2_out, not_1_out, not_2_out, not_3_out, not_4_out, not_5_out, not_6_out, slt_out;
  wire [2:0] or_1_out;

  not not_1 (not_1_out, funct[5]);
  not not_2 (not_2_out, funct[4]);
  not not_3 (not_3_out, funct[3]);
  not not_4 (not_4_out, funct[0]);
  not not_5 (not_5_out, funct[2]);
  not not_6 (not_6_out, funct[1]);
  and and_1 (and_1_out, funct[5], not_2_out, not_3_out, not_5_out, not_6_out, funct[0]);
  and and_2 (and_2_out, funct[5], not_2_out, not_3_out, not_5_out, funct[1], funct[0]);
  and slt (slt_out, funct[5], not_2_out, funct[3], not_5_out, funct[1], not_4_out);
  or or_1 (or_1_out[0], and_2_out, 1'b0);
  buf or_2 (or_1_out[1], 1'b0);  // OR_Gate
  or or_3 (or_1_out[2], slt_out, 1'b0);
  Multiplexer #(.width(3)) multiplexer_1 (.in0(aluOP), .in1(or_1_out), .out(opCode), .sel(isR));  // open: en

  // Notes on the sheet:
  //   addu
  //   subu
  //   alu0
  //   alu1
  //   alu2
endmodule

module BranchControl (
  input  zero,
  input  branchZero,
  input  [2:0] comp,
  input  [2:0] BranchComp,
  input  [4:0] rt,
  output branch
);

  wire and_1_out, bit_extender_1_out, branchcontrolcheck_1_enable, or_1_out;
  wire [2:0] and_2_out;

  Bit_Extender #(.in_width(5), .out_width(1)) bit_extender_1 (.in(rt), .out(bit_extender_1_out));
  and and_1 (and_1_out, zero, branchZero);
  assign and_2_out = comp & BranchComp;  // AND_Gate and_2, 3 bits wide
  BranchControlCheck branchcontrolcheck_1 (
    .cmp0(BranchComp[0]), .cmp1(BranchComp[1]), .cmp2(BranchComp[2]), .ckecker(bit_extender_1_out),
    .enable(branchcontrolcheck_1_enable));
  or or_1 (or_1_out, and_1_out, and_2_out[0], and_2_out[1], and_2_out[2]);
  and and_3 (branch, or_1_out, branchcontrolcheck_1_enable);
endmodule

module BranchControlCheck (
  input  cmp0,
  input  cmp1,
  input  cmp2,
  input  ckecker,
  output enable
);

  wire and_1_out, and_2_out, and_3_out, and_4_out, and_5_out, not_1_out, not_2_out, not_3_out, not_4_out,
       not_5_out, not_6_out;

  not not_1 (not_1_out, cmp0);
  and and_1 (and_1_out, not_1_out, not_2_out);
  not not_2 (not_2_out, cmp1);
  not not_3 (not_3_out, cmp1);
  and and_2 (and_2_out, not_3_out, not_4_out);
  not not_4 (not_4_out, ckecker);
  not not_5 (not_5_out, cmp0);
  and and_3 (and_3_out, not_5_out, ckecker);
  and and_4 (and_4_out, cmp1, not_6_out);
  not not_6 (not_6_out, cmp2);
  and and_5 (and_5_out, cmp0, cmp2);
  or or_1 (enable, and_1_out, and_2_out, and_3_out, and_4_out, and_5_out);
endmodule
